# Fritzing sketch PowerRegulator (saved by Fritzing 0.8.7b)

parts:
  proto1 = Adafruit_PermaProto_1_4_Board
  JP5 = Header 1 [package=1x01_offset]
  JP6 = Header 1 [package=1x01_offset]  # not connected
  JP1_GND = Header 1 [package=1x01_offset]
  JP8 = Header 1 [package=1x01_offset]
  IC1 = V_REG_LD1117VXX [package=78xxl]
  IC3 = Voltage Regulator [package=78xxl]
  C3 = Electrolytic Capacitor [capacitance=100µF voltage=20V package="200 mil [THT, electrolytic]"]  # not connected
  C4 = Electrolytic Capacitor [capacitance=100µF voltage=20V package="200 mil [THT, electrolytic]"]  # not connected
  C2 = Electrolytic Capacitor [capacitance=100µF voltage=20V package="200 mil [THT, electrolytic]"]  # not connected
  J1_3_3V_OUT = female pin header, 5 pins [form="♀ (female)"]  # not connected
  J5_5V_OUT_#1 = female pin header, 5 pins [form="♀ (female)"]  # not connected
  J8_5V_OUT_#2 = female pin header, 5 pins [form="♀ (female)"]  # not connected
  J4_GND_OUT = female pin header, 15 pins [form="♀ (female)"]  # not connected
  J9_12V_+ = female pin header, 5 pins [form="♀ (female)"]  # not connected
  J10_12VGND = female pin header, 5 pins [form="♀ (female)"]  # not connected
  S3 = SWITCH_SPDT [package=kps-1290]
  IC2 = Voltage Regulator [package=78xxl]

nets:
  N1: proto1.connectorE1, proto1.connectorF1
  N2: proto1.connectorE9, proto1.connectorF9
  N3: proto1.connectorE14, proto1.connectorF14
  N4: JP5.1, IC1.IN, IC3.IN, S3.O, IC2.IN
  GND: JP1_GND.1, IC1.GND, IC3.GND, IC2.GND
  N5: JP8.1, S3.S
