# Fritzing sketch Untitled Sketch 2 (saved by Fritzing 0.9.0b)
breadboards: 2

parts:
  Part1 = Arduino Mega 2560 (Rev3)
  IMU1 = Adafruit 10-DOF IMU Breakout
  M1 = DC Motor
  R2 = Rotary Potentiometer (Large) [maximum_resistance=100kΩ package=THT]
  R3 = Rotary Potentiometer (Large) [maximum_resistance=100kΩ package=THT]
  R4 = Rotary Potentiometer (Large) [maximum_resistance=100kΩ package=THT]
  M2 = DC Motor
  BATT1 = 4xAA Switchable Battery Pack w/Bare Wire
  BATT2 = 4xAA Switchable Battery Pack w/Bare Wire
  proto1 = Adafruit_PermaProto_1_4_Board
  J4 = female pin header, 6 pins [form="♀ (female)"]
  J3 = female pin header, 4 pins [form="♀ (female)"]
  U2 = LCD-16X2 [package=lcd-16x2_nosilk]

nets:
  N1: Part1.A0, R3.wiper
  N2: Part1.A1, R2.wiper
  N3: Part1.A2, R4.wiper
  N4: Part1.D21/SCL, IMU1.SCL
  N5: Part1.D20/SDA, IMU1.SDA
  N6: Part1.D18/TX1, U2.R_W
  N7: Part1.D14/TX3, J3.pin2
  5V: Part1.5V, IMU1.VIN, R2.leg1, R3.leg1, R4.leg1, U2.VDD
  GND: Part1.GND, IMU1.GND, R2.leg2, R3.leg2, R4.leg2, J3.pin4, U2.VO
  N8: M1.pin_1, J4.pin2
  N9: M1.pin_2, J4.pin1
  N10: M2.pin_1, J4.pin6
  N11: M2.pin_2, J4.pin5
  N12: BATT1.POS, BATT2.NEG
  N13: BATT1.NEG, proto1.connectorW8
  N14: BATT2.POS, J4.pin3
  N15: proto1.connectorZ10, J4.pin4

notes:
  Sabertooth 2x12

custom parts:
  4xAA Switchable Battery Pack w/Bare Wire: 4xAA Switchable Battery Pack with Bare Wire connection
